// Logisim project PC.circ as structural Verilog: 24 circuits, main circuit main
module main (
  input  [15:0] in_1,
  input  [15:0] in_2,
  output [15:0] out_3
);

  Subtractor #(.width(16)) subtractor_1 (.a(in_1), .b(in_2), .out(out_3));  // open: bin, bout
endmodule

module CAnd (
  input  in_1,
  input  in_2,
  output out_3
);

  wire nand_1_out;

  nand nand_1 (nand_1_out, in_1, in_2);
  nand nand_2 (out_3, nand_1_out, nand_1_out);
endmodule

module COR (
  input  in_1,
  input  in_2,
  output out_3
);

  wire nand_1_out, nand_2_out;

  nand nand_1 (nand_1_out, in_1, in_1);
  nand nand_2 (nand_2_out, in_2, in_2);
  nand nand_3 (out_3, nand_1_out, nand_2_out);
endmodule

module CNOT (
  input  in_1,
  output out_2
);

  nand nand_1 (out_2, in_1, in_1);
endmodule

module CXOR (
  input  in_1,
  input  in_2,
  output out_3
);

  wire nand_1_out, nand_2_out, nand_3_out;

  nand nand_1 (nand_1_out, in_1, in_2);
  nand nand_2 (nand_2_out, in_1, nand_1_out);
  nand nand_3 (nand_3_out, nand_1_out, in_2);
  nand nand_4 (out_3, nand_2_out, nand_3_out);
endmodule

module CMUX (
  input  in_1,
  input  in_2,
  input  in_3,
  output out_4
);

  wire and_1_out, xor_1_out;

  xor xor_1 (xor_1_out, in_1, in_3);
  and and_1 (and_1_out, in_2, in_3);
  or or_1 (out_4, xor_1_out, and_1_out);
endmodule

module CDMUX (
  input  in_1,
  input  in_2,
  output out_3,
  output out_4
);

  wire not_1_out;

  and and_1 (out_3, in_1, in_2);
  and and_2 (out_4, in_1, not_1_out);
  not not_1 (not_1_out, in_2);
endmodule

module MUX4WAY16 (
  input  [15:0] A,
  input  [15:0] B,
  input  [15:0] C,
  input  [15:0] D,
  input  [1:0] in_5,
  output [15:0] out_6
);

  wire not_1_out, splitter2_1_out_2, splitter2_1_out_3;
  wire [15:0] mux16_1_o, mux16_2_o, mux16_3_o, mux16_4_o, mux16_5_o, mux16_6_o;

  MUX16 mux16_1 (.S(not_1_out), .A(A), .O(mux16_1_o));  // open: B
  MUX16 mux16_2 (.S(not_1_out), .A(B), .O(mux16_2_o));  // open: B
  MUX16 mux16_3 (.S(not_1_out), .B(C), .O(mux16_3_o));  // open: A
  MUX16 mux16_4 (.S(not_1_out), .B(D), .O(mux16_4_o));  // open: A
  not not_1 (not_1_out, splitter2_1_out_2);
  SPLITTER2 splitter2_1 (.in_1(in_5), .out_3(splitter2_1_out_3), .out_2(splitter2_1_out_2));
  MUX16 mux16_5 (.S(splitter2_1_out_3), .A(mux16_2_o), .B(mux16_1_o), .O(mux16_5_o));
  MUX16 mux16_6 (.S(splitter2_1_out_3), .A(mux16_4_o), .B(mux16_3_o), .O(mux16_6_o));
  assign out_6 = mux16_5_o | mux16_6_o;  // OR_Gate or_1, 16 bits wide
endmodule

module MUX16 (
  input  S,
  input  [15:0] A,
  input  [15:0] B,
  output [15:0] O
);

  wire and_1_out, and_2_out, and_3_out, and_4_out, and_5_out, and_6_out, and_7_out, and_8_out, and_9_out,
       and_10_out, and_11_out, and_12_out, and_13_out, and_14_out, and_15_out, and_16_out, and_17_out,
       and_18_out, and_19_out, and_20_out, and_21_out, and_22_out, and_23_out, and_24_out, and_25_out,
       and_26_out, and_27_out, and_28_out, and_29_out, and_30_out, and_31_out, and_32_out, not_1_out,
       splitter16_1_out_2, splitter16_1_out_3, splitter16_1_out_4, splitter16_1_out_5, splitter16_1_out_6,
       splitter16_1_out_7, splitter16_1_out_8, splitter16_1_out_9, splitter16_1_out_10, splitter16_1_out_11,
       splitter16_1_out_12, splitter16_1_out_13, splitter16_1_out_14, splitter16_1_out_15,
       splitter16_1_out_16, splitter16_1_out_17, splitter16_2_out_2, splitter16_2_out_3, splitter16_2_out_4,
       splitter16_2_out_5, splitter16_2_out_6, splitter16_2_out_7, splitter16_2_out_8, splitter16_2_out_9,
       splitter16_2_out_10, splitter16_2_out_11, splitter16_2_out_12, splitter16_2_out_13,
       splitter16_2_out_14, splitter16_2_out_15, splitter16_2_out_16, splitter16_2_out_17;
  wire [15:0] merger16_1_out_17, merger16_2_out_17;

  Splitter16 splitter16_1 (
    .in_1(A), .out_3(splitter16_1_out_3), .out_4(splitter16_1_out_4), .out_5(splitter16_1_out_5),
    .out_6(splitter16_1_out_6), .out_7(splitter16_1_out_7), .out_8(splitter16_1_out_8),
    .out_9(splitter16_1_out_9), .out_10(splitter16_1_out_10), .out_11(splitter16_1_out_11),
    .out_12(splitter16_1_out_12), .out_13(splitter16_1_out_13), .out_14(splitter16_1_out_14),
    .out_15(splitter16_1_out_15), .out_16(splitter16_1_out_16), .out_17(splitter16_1_out_17),
    .out_2(splitter16_1_out_2));
  Splitter16 splitter16_2 (
    .in_1(B), .out_3(splitter16_2_out_3), .out_4(splitter16_2_out_4), .out_5(splitter16_2_out_5),
    .out_6(splitter16_2_out_6), .out_7(splitter16_2_out_7), .out_8(splitter16_2_out_8),
    .out_9(splitter16_2_out_9), .out_10(splitter16_2_out_10), .out_11(splitter16_2_out_11),
    .out_12(splitter16_2_out_12), .out_13(splitter16_2_out_13), .out_14(splitter16_2_out_14),
    .out_15(splitter16_2_out_15), .out_16(splitter16_2_out_16), .out_17(splitter16_2_out_17),
    .out_2(splitter16_2_out_2));
  not not_1 (not_1_out, S);
  and and_1 (and_1_out, S, splitter16_1_out_2);
  and and_2 (and_2_out, S, splitter16_1_out_3);
  and and_3 (and_3_out, S, splitter16_1_out_4);
  and and_4 (and_4_out, S, splitter16_1_out_5);
  and and_5 (and_5_out, S, splitter16_1_out_6);
  and and_6 (and_6_out, S, splitter16_1_out_7);
  and and_7 (and_7_out, S, splitter16_1_out_8);
  and and_8 (and_8_out, S, splitter16_1_out_9);
  and and_9 (and_9_out, S, splitter16_1_out_10);
  and and_10 (and_10_out, S, splitter16_1_out_11);
  and and_11 (and_11_out, S, splitter16_1_out_12);
  and and_12 (and_12_out, S, splitter16_1_out_13);
  and and_13 (and_13_out, S, splitter16_1_out_14);
  and and_14 (and_14_out, S, splitter16_1_out_15);
  and and_15 (and_15_out, S, splitter16_1_out_16);
  and and_16 (and_16_out, S, splitter16_1_out_17);
  and and_17 (and_17_out, not_1_out, splitter16_2_out_2);
  and and_18 (and_18_out, not_1_out, splitter16_2_out_3);
  and and_19 (and_19_out, not_1_out, splitter16_2_out_4);
  and and_20 (and_20_out, not_1_out, splitter16_2_out_5);
  and and_21 (and_21_out, not_1_out, splitter16_2_out_6);
  and and_22 (and_22_out, not_1_out, splitter16_2_out_7);
  and and_23 (and_23_out, not_1_out, splitter16_2_out_8);
  and and_24 (and_24_out, not_1_out, splitter16_2_out_9);
  and and_25 (and_25_out, not_1_out, splitter16_2_out_10);
  and and_26 (and_26_out, not_1_out, splitter16_2_out_11);
  and and_27 (and_27_out, not_1_out, splitter16_2_out_12);
  and and_28 (and_28_out, not_1_out, splitter16_2_out_13);
  and and_29 (and_29_out, not_1_out, splitter16_2_out_14);
  and and_30 (and_30_out, not_1_out, splitter16_2_out_15);
  and and_31 (and_31_out, not_1_out, splitter16_2_out_16);
  and and_32 (and_32_out, not_1_out, splitter16_2_out_17);
  Merger16 merger16_1 (
    .in_2(and_2_out), .in_3(and_3_out), .in_4(and_4_out), .in_5(and_5_out), .in_6(and_6_out),
    .in_7(and_7_out), .in_8(and_8_out), .in_9(and_9_out), .in_10(and_10_out), .in_11(and_11_out),
    .in_1(and_1_out), .in_12(and_12_out), .in_13(and_13_out), .in_14(and_14_out), .in_15(and_15_out),
    .in_16(and_16_out), .out_17(merger16_1_out_17));
  Merger16 merger16_2 (
    .in_2(and_18_out), .in_3(and_19_out), .in_4(and_20_out), .in_5(and_21_out), .in_6(and_22_out),
    .in_7(and_23_out), .in_8(and_24_out), .in_9(and_25_out), .in_10(and_26_out), .in_11(and_27_out),
    .in_1(and_17_out), .in_12(and_28_out), .in_13(and_29_out), .in_14(and_30_out), .in_15(and_31_out),
    .in_16(and_32_out), .out_17(merger16_2_out_17));
  assign O = merger16_1_out_17 ^ merger16_2_out_17;  // XOR_Gate xor_1, 16 bits wide
endmodule

module AND16 (
  input  [15:0] A,
  input  [15:0] B,
  output [15:0] out_3
);

  wire and_1_out, and_3_out, and_4_out, and_5_out, and_6_out, and_11_out, and_12_out, and_13_out,
       splitter16_1_out_2, splitter16_1_out_3, splitter16_1_out_4, splitter16_1_out_5, splitter16_1_out_6,
       splitter16_1_out_7, splitter16_1_out_8, splitter16_1_out_9, splitter16_1_out_10, splitter16_1_out_11,
       splitter16_1_out_12, splitter16_1_out_13, splitter16_1_out_14, splitter16_1_out_15,
       splitter16_1_out_16, splitter16_1_out_17, splitter16_2_out_2, splitter16_2_out_3, splitter16_2_out_4,
       splitter16_2_out_5, splitter16_2_out_6, splitter16_2_out_7, splitter16_2_out_8, splitter16_2_out_9,
       splitter16_2_out_10, splitter16_2_out_11, splitter16_2_out_12, splitter16_2_out_13,
       splitter16_2_out_14, splitter16_2_out_15, splitter16_2_out_16, splitter16_2_out_17;

  Splitter16 splitter16_1 (
    .in_1(A), .out_3(splitter16_1_out_3), .out_4(splitter16_1_out_4), .out_5(splitter16_1_out_5),
    .out_6(splitter16_1_out_6), .out_7(splitter16_1_out_7), .out_8(splitter16_1_out_8),
    .out_9(splitter16_1_out_9), .out_10(splitter16_1_out_10), .out_11(splitter16_1_out_11),
    .out_12(splitter16_1_out_12), .out_13(splitter16_1_out_13), .out_14(splitter16_1_out_14),
    .out_15(splitter16_1_out_15), .out_16(splitter16_1_out_16), .out_17(splitter16_1_out_17),
    .out_2(splitter16_1_out_2));
  Splitter16 splitter16_2 (
    .in_1(B), .out_3(splitter16_2_out_3), .out_4(splitter16_2_out_4), .out_5(splitter16_2_out_5),
    .out_6(splitter16_2_out_6), .out_7(splitter16_2_out_7), .out_8(splitter16_2_out_8),
    .out_9(splitter16_2_out_9), .out_10(splitter16_2_out_10), .out_11(splitter16_2_out_11),
    .out_12(splitter16_2_out_12), .out_13(splitter16_2_out_13), .out_14(splitter16_2_out_14),
    .out_15(splitter16_2_out_15), .out_16(splitter16_2_out_16), .out_17(splitter16_2_out_17),
    .out_2(splitter16_2_out_2));
  and and_1 (and_1_out, splitter16_1_out_2, splitter16_2_out_2);
  // AND_Gate and_2 has open pins: in0=splitter16_1_out_10, in1=splitter16_2_out_10, out=open
  and and_3 (and_3_out, splitter16_1_out_3, splitter16_2_out_3);
  and and_4 (and_4_out, splitter16_1_out_4, splitter16_2_out_4);
  and and_5 (and_5_out, splitter16_1_out_5, splitter16_2_out_5);
  and and_6 (and_6_out, splitter16_1_out_6, splitter16_2_out_6);
  // AND_Gate and_7 has open pins: in0=splitter16_1_out_11, in1=splitter16_2_out_11, out=open
  // AND_Gate and_8 has open pins: in0=splitter16_1_out_12, in1=splitter16_2_out_12, out=open
  // AND_Gate and_9 has open pins: in0=splitter16_1_out_13, in1=splitter16_2_out_13, out=open
  // AND_Gate and_10 has open pins: in0=splitter16_1_out_14, in1=splitter16_2_out_14, out=open
  and and_11 (and_11_out, splitter16_1_out_7, splitter16_2_out_7);
  and and_12 (and_12_out, splitter16_1_out_8, splitter16_2_out_8);
  and and_13 (and_13_out, splitter16_1_out_9, splitter16_2_out_9);
  // AND_Gate and_14 has open pins: in0=splitter16_1_out_15, in1=splitter16_2_out_15, out=open
  // AND_Gate and_15 has open pins: in0=splitter16_1_out_16, in1=splitter16_2_out_16, out=open
  // AND_Gate and_16 has open pins: in0=splitter16_1_out_17, in1=splitter16_2_out_17, out=open
  Merger16 merger16_1 (
    .in_2(and_3_out), .in_3(and_4_out), .in_4(and_5_out), .in_5(and_6_out), .in_6(and_11_out),
    .in_7(and_12_out), .in_8(and_13_out), .in_1(and_1_out), .out_17(out_3));  // open: in_9, in_10, in_11, in_12, in_13, in_14, in_15, in_16
endmodule

module Splitter16 (
  input  [15:0] in_1,
  output out_2,
  output out_3,
  output out_4,
  output out_5,
  output out_6,
  output out_7,
  output out_8,
  output out_9,
  output out_10,
  output out_11,
  output out_12,
  output out_13,
  output out_14,
  output out_15,
  output out_16,
  output out_17
);

  BitSelector #(.width(16)) bitselector_1 (.in(in_1), .out(out_2), .sel(4'b0000));
  BitSelector #(.width(16)) bitselector_2 (.in(in_1), .out(out_3), .sel(4'b0001));
  BitSelector #(.width(16)) bitselector_3 (.in(in_1), .out(out_4), .sel(4'b0010));
  BitSelector #(.width(16)) bitselector_4 (.in(in_1), .out(out_5), .sel(4'b0011));
  BitSelector #(.width(16)) bitselector_5 (.in(in_1), .out(out_6), .sel(4'b0100));
  BitSelector #(.width(16)) bitselector_6 (.in(in_1), .out(out_7), .sel(4'b0101));
  BitSelector #(.width(16)) bitselector_7 (.in(in_1), .out(out_8), .sel(4'b0110));
  BitSelector #(.width(16)) bitselector_8 (.in(in_1), .out(out_9), .sel(4'b0111));
  BitSelector #(.width(16)) bitselector_9 (.in(in_1), .out(out_10), .sel(4'b1000));
  BitSelector #(.width(16)) bitselector_10 (.in(in_1), .out(out_11), .sel(4'b1001));
  BitSelector #(.width(16)) bitselector_11 (.in(in_1), .out(out_12), .sel(4'b1010));
  BitSelector #(.width(16)) bitselector_12 (.in(in_1), .out(out_13), .sel(4'b1011));
  BitSelector #(.width(16)) bitselector_13 (.in(in_1), .out(out_14), .sel(4'b1100));
  BitSelector #(.width(16)) bitselector_14 (.in(in_1), .out(out_15), .sel(4'b1101));
  BitSelector #(.width(16)) bitselector_15 (.in(in_1), .out(out_16), .sel(4'b1111));
  BitSelector #(.width(16)) bitselector_16 (.in(in_1), .out(out_17), .sel(4'b1111));
endmodule

module Splitter4 (
  input  [3:0] in_1,
  output out_2,
  output out_3,
  output out_4,
  output out_5
);

  BitSelector #(.width(4)) bitselector_1 (.in(in_1), .out(out_2), .sel(2'b00));
  BitSelector #(.width(4)) bitselector_2 (.in(in_1), .out(out_3), .sel(2'b01));
  BitSelector #(.width(4)) bitselector_3 (.in(in_1), .out(out_4), .sel(2'b10));
  BitSelector #(.width(4)) bitselector_4 (.in(in_1), .out(out_5), .sel(2'b11));
endmodule

module Merger16 (
  input  in_1,
  input  in_2,
  input  in_3,
  input  in_4,
  input  in_5,
  input  in_6,
  input  in_7,
  input  in_8,
  input  in_9,
  input  in_10,
  input  in_11,
  input  in_12,
  input  in_13,
  input  in_14,
  input  in_15,
  input  in_16,
  output [15:0] out_17
);

  wire [15:0] pla_1_out, pla_2_out, pla_3_out, pla_4_out, pla_5_out, pla_6_out, pla_7_out, pla_8_out,
       pla_9_out, pla_10_out, pla_11_out, pla_12_out, pla_13_out, pla_14_out, pla_15_out, pla_16_out;

  PLA #(.in_width(1), .out_width(16), .\table ("0 0000000000000000\n1 0000000000000001")) pla_1 (
    .in(in_1), .out(pla_1_out));
  PLA #(.in_width(1), .out_width(16), .\table ("0 0000000000000000\n1 0000000000000010")) pla_2 (
    .in(in_2), .out(pla_2_out));
  PLA #(.in_width(1), .out_width(16), .\table ("0 0000000000000000\n1 0000000000000100")) pla_3 (
    .in(in_3), .out(pla_3_out));
  PLA #(.in_width(1), .out_width(16), .\table ("0 0000000000000000\n1 0000000000001000")) pla_4 (
    .in(in_4), .out(pla_4_out));
  PLA #(.in_width(1), .out_width(16), .\table ("0 0000000000000000\n1 0000000000010000")) pla_5 (
    .in(in_5), .out(pla_5_out));
  PLA #(.in_width(1), .out_width(16), .\table ("0 0000000000000000\n1 0000000000100000")) pla_6 (
    .in(in_6), .out(pla_6_out));
  PLA #(.in_width(1), .out_width(16), .\table ("0 0000000000000000\n1 0000000001000000")) pla_7 (
    .in(in_7), .out(pla_7_out));
  PLA #(.in_width(1), .out_width(16), .\table ("0 0000000000000000\n1 0000000010000000")) pla_8 (
    .in(in_8), .out(pla_8_out));
  PLA #(.in_width(1), .out_width(16), .\table ("0 0000000000000000\n1 0000000100000000")) pla_9 (
    .in(in_9), .out(pla_9_out));
  PLA #(.in_width(1), .out_width(16), .\table ("0 0000000000000000\n1 0000001000000000")) pla_10 (
    .in(in_10), .out(pla_10_out));
  PLA #(.in_width(1), .out_width(16), .\table ("0 0000000000000000\n1 0000010000000000")) pla_11 (
    .in(in_11), .out(pla_11_out));
  PLA #(.in_width(1), .out_width(16), .\table ("0 0000000000000000\n1 0000100000000000")) pla_12 (
    .in(in_12), .out(pla_12_out));
  PLA #(.in_width(1), .out_width(16), .\table ("0 0000000000000000\n1 0001000000000000")) pla_13 (
    .in(in_13), .out(pla_13_out));
  PLA #(.in_width(1), .out_width(16), .\table ("0 0000000000000000\n1 0010000000000000")) pla_14 (
    .in(in_14), .out(pla_14_out));
  PLA #(.in_width(1), .out_width(16), .\table ("0 0000000000000000\n1 0100000000000000")) pla_15 (
    .in(in_15), .out(pla_15_out));
  PLA #(.in_width(1), .out_width(16), .\table ("0 0000000000000000\n1 1000000000000000")) pla_16 (
    .in(in_16), .out(pla_16_out));
  assign out_17 = pla_1_out | pla_2_out | pla_3_out | pla_4_out | pla_5_out | pla_6_out | pla_7_out | pla_8_out | pla_9_out | pla_10_out | pla_11_out | pla_12_out | pla_13_out | pla_14_out | pla_15_out | pla_16_out;  // OR_Gate or_1, 16 bits wide
endmodule

module Merger4 (
  input  in_1,
  input  in_2,
  input  in_3,
  input  in_4,
  output out_5
);

  or or_1 (out_5, in_4, in_3);
  // OR_Gate or_2 has open pins: in0=in_4, in1=in_2, out=open
endmodule

module SPLITTER2 (
  input  [1:0] in_1,
  output out_2,
  output out_3
);

  BitSelector #(.width(2)) bitselector_1 (.in(in_1), .out(out_2), .sel(1'b0));
  BitSelector #(.width(2)) bitselector_2 (.in(in_1), .out(out_3), .sel(1'b1));
endmodule

module DMUX16 (
  input  [15:0] in_1,
  input  in_2,
  output [15:0] out_3,
  output [15:0] out_4
);

  wire and_1_out, and_2_out, and_3_out, and_4_out, and_5_out, and_6_out, and_7_out, and_8_out, and_9_out,
       and_10_out, and_11_out, and_12_out, and_13_out, and_14_out, and_15_out, and_16_out, and_17_out,
       and_18_out, and_19_out, and_20_out, and_21_out, and_22_out, and_23_out, and_24_out, and_25_out,
       and_26_out, and_27_out, and_28_out, and_29_out, and_30_out, and_31_out, and_32_out, not_1_out,
       splitter16_1_out_2, splitter16_1_out_3, splitter16_1_out_4, splitter16_1_out_5, splitter16_1_out_6,
       splitter16_1_out_7, splitter16_1_out_8, splitter16_1_out_9, splitter16_1_out_10, splitter16_1_out_11,
       splitter16_1_out_12, splitter16_1_out_13, splitter16_1_out_14, splitter16_1_out_15,
       splitter16_1_out_16, splitter16_1_out_17;

  Splitter16 splitter16_1 (
    .in_1(in_1), .out_3(splitter16_1_out_3), .out_4(splitter16_1_out_4), .out_5(splitter16_1_out_5),
    .out_6(splitter16_1_out_6), .out_7(splitter16_1_out_7), .out_8(splitter16_1_out_8),
    .out_9(splitter16_1_out_9), .out_10(splitter16_1_out_10), .out_11(splitter16_1_out_11),
    .out_12(splitter16_1_out_12), .out_13(splitter16_1_out_13), .out_14(splitter16_1_out_14),
    .out_15(splitter16_1_out_15), .out_16(splitter16_1_out_16), .out_17(splitter16_1_out_17),
    .out_2(splitter16_1_out_2));
  not not_1 (not_1_out, in_2);
  and and_1 (and_1_out, splitter16_1_out_2, not_1_out);
  and and_2 (and_2_out, splitter16_1_out_3, not_1_out);
  and and_3 (and_3_out, splitter16_1_out_4, not_1_out);
  and and_4 (and_4_out, splitter16_1_out_5, not_1_out);
  and and_5 (and_5_out, splitter16_1_out_6, not_1_out);
  and and_6 (and_6_out, splitter16_1_out_7, not_1_out);
  and and_7 (and_7_out, splitter16_1_out_8, not_1_out);
  and and_8 (and_8_out, splitter16_1_out_9, not_1_out);
  and and_9 (and_9_out, splitter16_1_out_10, not_1_out);
  and and_10 (and_10_out, splitter16_1_out_11, not_1_out);
  and and_11 (and_11_out, splitter16_1_out_12, not_1_out);
  and and_12 (and_12_out, splitter16_1_out_13, not_1_out);
  and and_13 (and_13_out, splitter16_1_out_14, not_1_out);
  and and_14 (and_14_out, splitter16_1_out_15, not_1_out);
  and and_15 (and_15_out, splitter16_1_out_16, not_1_out);
  and and_16 (and_16_out, splitter16_1_out_17, not_1_out);
  and and_17 (and_17_out, in_2, splitter16_1_out_2);
  and and_18 (and_18_out, in_2, splitter16_1_out_3);
  and and_19 (and_19_out, in_2, splitter16_1_out_4);
  and and_20 (and_20_out, in_2, splitter16_1_out_5);
  and and_21 (and_21_out, in_2, splitter16_1_out_6);
  and and_22 (and_22_out, in_2, splitter16_1_out_7);
  and and_23 (and_23_out, in_2, splitter16_1_out_8);
  and and_24 (and_24_out, in_2, splitter16_1_out_9);
  and and_25 (and_25_out, in_2, splitter16_1_out_10);
  and and_26 (and_26_out, in_2, splitter16_1_out_11);
  and and_27 (and_27_out, in_2, splitter16_1_out_12);
  and and_28 (and_28_out, in_2, splitter16_1_out_13);
  and and_29 (and_29_out, in_2, splitter16_1_out_14);
  and and_30 (and_30_out, in_2, splitter16_1_out_15);
  and and_31 (and_31_out, in_2, splitter16_1_out_16);
  and and_32 (and_32_out, in_2, splitter16_1_out_17);
  Merger16 merger16_1 (
    .in_2(and_2_out), .in_3(and_3_out), .in_4(and_4_out), .in_5(and_5_out), .in_6(and_6_out),
    .in_7(and_7_out), .in_8(and_8_out), .in_9(and_9_out), .in_10(and_10_out), .in_11(and_11_out),
    .in_1(and_1_out), .in_12(and_12_out), .in_13(and_13_out), .in_14(and_14_out), .in_15(and_15_out),
    .in_16(and_16_out), .out_17(out_3));
  Merger16 merger16_2 (
    .in_2(and_18_out), .in_3(and_19_out), .in_4(and_20_out), .in_5(and_21_out), .in_6(and_22_out),
    .in_7(and_23_out), .in_8(and_24_out), .in_9(and_25_out), .in_10(and_26_out), .in_11(and_27_out),
    .in_1(and_17_out), .in_12(and_28_out), .in_13(and_29_out), .in_14(and_30_out), .in_15(and_31_out),
    .in_16(and_32_out), .out_17(out_4));
endmodule

module DMUX4WAY16 (
  input  [15:0] in_1,
  input  [1:0] in_2,
  output [15:0] out_3,
  output [15:0] out_4,
  output [15:0] out_5,
  output [15:0] out_6
);

  wire splitter2_1_out_2, splitter2_1_out_3;
  wire [15:0] dmux16_1_out_3, dmux16_1_out_4;

  DMUX16 dmux16_1 (.in_2(splitter2_1_out_3), .in_1(in_1), .out_3(dmux16_1_out_3), .out_4(dmux16_1_out_4));
  SPLITTER2 splitter2_1 (.in_1(in_2), .out_3(splitter2_1_out_3), .out_2(splitter2_1_out_2));
  DMUX16 dmux16_2 (.in_2(splitter2_1_out_2), .in_1(dmux16_1_out_3), .out_3(out_3), .out_4(out_4));
  DMUX16 dmux16_3 (.in_2(splitter2_1_out_2), .in_1(dmux16_1_out_4), .out_3(out_5), .out_4(out_6));
endmodule

module DMUX8WAY (
  input  in_1,
  input  [2:0] in_2,
  output out_3,
  output out_4,
  output out_5,
  output out_6,
  output out_7,
  output out_8,
  output out_9,
  output out_10
);

  wire cdmux_1_out_3, cdmux_1_out_4, cdmux_2_out_3, cdmux_2_out_4, cdmux_3_out_3, cdmux_3_out_4,
       splitter3_1_out_2, splitter3_1_out_3, splitter3_1_out_4;

  CDMUX cdmux_1 (.in_2(splitter3_1_out_4), .in_1(in_1), .out_3(cdmux_1_out_3), .out_4(cdmux_1_out_4));
  SPLITTER3 splitter3_1 (.in_1(in_2), .out_3(splitter3_1_out_3), .out_4(splitter3_1_out_4), .out_2(splitter3_1_out_2));
  CDMUX cdmux_2 (.in_2(splitter3_1_out_3), .in_1(cdmux_1_out_3), .out_3(cdmux_2_out_3), .out_4(cdmux_2_out_4));
  CDMUX cdmux_3 (.in_2(splitter3_1_out_3), .in_1(cdmux_1_out_4), .out_3(cdmux_3_out_3), .out_4(cdmux_3_out_4));
  CDMUX cdmux_4 (.in_2(splitter3_1_out_2), .in_1(cdmux_2_out_3), .out_3(out_3), .out_4(out_4));
  CDMUX cdmux_5 (.in_2(splitter3_1_out_2), .in_1(cdmux_2_out_4), .out_3(out_5), .out_4(out_6));
  CDMUX cdmux_6 (.in_2(splitter3_1_out_2), .in_1(cdmux_3_out_3), .out_3(out_7), .out_4(out_8));
  CDMUX cdmux_7 (.in_2(splitter3_1_out_2), .in_1(cdmux_3_out_4), .out_3(out_9), .out_4(out_10));
endmodule

module SPLITTER3 (
  input  [2:0] in_1,
  output out_2,
  output out_3,
  output out_4
);

  BitSelector #(.width(3)) bitselector_1 (.in(in_1), .out(out_2), .sel(2'b00));
  BitSelector #(.width(3)) bitselector_2 (.in(in_1), .out(out_3), .sel(2'b01));
  BitSelector #(.width(3)) bitselector_3 (.in(in_1), .out(out_4), .sel(2'b10));
endmodule

module DMUX4WAY (
  input  in_1,
  input  [1:0] in_2,
  output out_3,
  output out_4,
  output out_5,
  output out_6
);

  wire cdmux_1_out_3, cdmux_1_out_4, splitter2_1_out_2, splitter2_1_out_3;

  CDMUX cdmux_1 (.in_2(splitter2_1_out_3), .in_1(in_1), .out_3(cdmux_1_out_3), .out_4(cdmux_1_out_4));
  SPLITTER2 splitter2_1 (.in_1(in_2), .out_3(splitter2_1_out_3), .out_2(splitter2_1_out_2));
  CDMUX cdmux_2 (.in_2(splitter2_1_out_2), .in_1(cdmux_1_out_3), .out_3(out_3), .out_4(out_4));
  CDMUX cdmux_3 (.in_2(splitter2_1_out_2), .in_1(cdmux_1_out_4), .out_3(out_5), .out_4(out_6));
endmodule

module HALFADDER (
  input  in_1,
  input  in_2,
  output out_3,
  output out_4
);

  xor xor_1 (out_3, in_1, in_2);
  and and_1 (out_4, in_1, in_2);
endmodule

module FULLADDER (
  input  in_1,
  input  in_2,
  input  in_3,
  output out_4,
  output out_5
);

  wire and_1_out, and_2_out, xor_1_out;

  xor xor_1 (xor_1_out, in_1, in_2);
  and and_1 (and_1_out, in_1, in_2);
  xor xor_2 (out_4, xor_1_out, in_3);
  and and_2 (and_2_out, xor_1_out, in_3);
  xor xor_3 (out_5, and_2_out, and_1_out);
endmodule

module CADDER (
  input  [15:0] in_1,
  input  [15:0] in_2,
  output [15:0] out_3,
  output out_4
);

  wire fulladder_1_out_5, fulladder_2_out_5, fulladder_3_out_5, fulladder_4_out_5, fulladder_5_out_5,
       fulladder_6_out_5, fulladder_7_out_5, fulladder_8_out_5, fulladder_9_out_5, fulladder_10_out_5,
       fulladder_11_out_5, fulladder_12_out_5, fulladder_13_out_5, fulladder_14_out_5, halfadder_1_out_4;

  HALFADDER halfadder_1 (.in_1(in_1[0]), .in_2(in_2[0]), .out_4(halfadder_1_out_4), .out_3(out_3[0]));
  FULLADDER fulladder_1 (
    .in_3(in_2[1]), .in_1(halfadder_1_out_4), .in_2(in_1[1]), .out_4(out_3[1]), .out_5(fulladder_1_out_5));
  FULLADDER fulladder_2 (
    .in_3(in_2[2]), .in_1(fulladder_1_out_5), .in_2(in_1[2]), .out_4(out_3[2]), .out_5(fulladder_2_out_5));
  FULLADDER fulladder_3 (
    .in_3(in_2[3]), .in_1(fulladder_2_out_5), .in_2(in_1[3]), .out_4(out_3[3]), .out_5(fulladder_3_out_5));
  FULLADDER fulladder_4 (
    .in_3(in_2[4]), .in_1(fulladder_3_out_5), .in_2(in_1[4]), .out_4(out_3[4]), .out_5(fulladder_4_out_5));
  FULLADDER fulladder_5 (
    .in_3(in_2[5]), .in_1(fulladder_4_out_5), .in_2(in_1[5]), .out_4(out_3[5]), .out_5(fulladder_5_out_5));
  FULLADDER fulladder_6 (
    .in_3(in_2[6]), .in_1(fulladder_5_out_5), .in_2(in_1[6]), .out_4(out_3[6]), .out_5(fulladder_6_out_5));
  FULLADDER fulladder_7 (
    .in_3(in_2[7]), .in_1(fulladder_6_out_5), .in_2(in_1[7]), .out_4(out_3[7]), .out_5(fulladder_7_out_5));
  FULLADDER fulladder_8 (
    .in_3(in_2[8]), .in_1(fulladder_7_out_5), .in_2(in_1[8]), .out_4(out_3[8]), .out_5(fulladder_8_out_5));
  FULLADDER fulladder_9 (
    .in_3(in_2[9]), .in_1(fulladder_8_out_5), .in_2(in_1[9]), .out_4(out_3[9]), .out_5(fulladder_9_out_5));
  FULLADDER fulladder_10 (
    .in_3(in_2[10]), .in_1(fulladder_9_out_5), .in_2(in_1[10]), .out_4(out_3[10]), .out_5(fulladder_10_out_5));
  FULLADDER fulladder_11 (
    .in_3(in_2[11]), .in_1(fulladder_10_out_5), .in_2(in_1[11]), .out_4(out_3[11]), .out_5(fulladder_11_out_5));
  FULLADDER fulladder_12 (
    .in_3(in_2[12]), .in_1(fulladder_11_out_5), .in_2(in_1[12]), .out_4(out_3[12]), .out_5(fulladder_12_out_5));
  FULLADDER fulladder_13 (
    .in_3(in_2[13]), .in_1(fulladder_12_out_5), .in_2(in_1[13]), .out_4(out_3[13]), .out_5(fulladder_13_out_5));
  FULLADDER fulladder_14 (
    .in_3(in_2[14]), .in_1(fulladder_13_out_5), .in_2(in_1[14]), .out_4(out_3[14]), .out_5(fulladder_14_out_5));
  FULLADDER fulladder_15 (
    .in_3(in_2[15]), .in_1(fulladder_14_out_5), .in_2(in_1[15]), .out_4(out_3[15]), .out_5(out_4));
endmodule

module ALU (
  input  [15:0] x,
  input  zx,
  input  nx,
  input  [15:0] y,
  input  zy,
  input  ny,
  input  f,
  input  no,
  output ng,
  output zr,
  output [15:0] ruedi
);

  wire [15:0] adder_1_out, and_1_out, demultiplexer_1_out0, demultiplexer_2_out0, demultiplexer_3_out0,
       demultiplexer_3_out1, demultiplexer_4_out0, demultiplexer_4_out1, demultiplexer_5_out0,
       demultiplexer_5_out1, demultiplexer_6_out0, demultiplexer_6_out1, demultiplexer_7_out0,
       demultiplexer_7_out1, demultiplexer_8_out0, demultiplexer_8_out1, demultiplexer_9_out0,
       demultiplexer_9_out1, multiplexer_1_out, multiplexer_2_out, multiplexer_3_out, multiplexer_4_out,
       multiplexer_5_out, multiplexer_6_out, multiplexer_7_out, not_1_out, not_2_out, not_3_out, not_4_out,
       not_5_out;

  Demultiplexer #(.width(16)) demultiplexer_1 (.out0(demultiplexer_1_out0), .in(x), .sel(zx));  // open: out1
  Demultiplexer #(.width(16)) demultiplexer_2 (.out0(demultiplexer_2_out0), .in(y), .sel(zy));  // open: out1
  Demultiplexer #(.width(16)) demultiplexer_3 (
    .out0(demultiplexer_3_out0), .out1(demultiplexer_3_out1), .in(demultiplexer_1_out0), .sel(nx));
  Demultiplexer #(.width(16)) demultiplexer_4 (
    .out0(demultiplexer_4_out0), .out1(demultiplexer_4_out1), .in({16{1'b0}}), .sel(nx));
  Demultiplexer #(.width(16)) demultiplexer_5 (
    .out0(demultiplexer_5_out0), .out1(demultiplexer_5_out1), .in(demultiplexer_2_out0), .sel(ny));
  Demultiplexer #(.width(16)) demultiplexer_6 (
    .out0(demultiplexer_6_out0), .out1(demultiplexer_6_out1), .in({16{1'b0}}), .sel(ny));
  assign not_1_out = ~demultiplexer_3_out1;  // NOT_Gate not_1, 16 bits wide
  assign not_2_out = ~demultiplexer_4_out1;  // NOT_Gate not_2, 16 bits wide
  assign not_3_out = ~demultiplexer_5_out1;  // NOT_Gate not_3, 16 bits wide
  assign not_4_out = ~demultiplexer_6_out1;  // NOT_Gate not_4, 16 bits wide
  Multiplexer #(.width(16)) multiplexer_1 (
    .in0(demultiplexer_3_out0), .in1(not_1_out), .out(multiplexer_1_out), .sel(nx));
  Multiplexer #(.width(16)) multiplexer_2 (
    .in0(demultiplexer_4_out0), .in1(not_2_out), .out(multiplexer_2_out), .sel(nx));
  Multiplexer #(.width(16)) multiplexer_3 (
    .in0(demultiplexer_5_out0), .in1(not_3_out), .out(multiplexer_3_out), .sel(ny));
  Multiplexer #(.width(16)) multiplexer_4 (
    .in0(demultiplexer_6_out0), .in1(not_4_out), .out(multiplexer_4_out), .sel(ny));
  Multiplexer #(.width(16)) multiplexer_5 (
    .in0(multiplexer_1_out), .in1(multiplexer_2_out), .out(multiplexer_5_out), .sel(zx));
  Demultiplexer #(.width(16)) demultiplexer_7 (
    .out0(demultiplexer_7_out0), .out1(demultiplexer_7_out1), .in(multiplexer_5_out), .sel(f));
  Multiplexer #(.width(16)) multiplexer_6 (
    .in0(multiplexer_3_out), .in1(multiplexer_4_out), .out(multiplexer_6_out), .sel(zy));
  Demultiplexer #(.width(16)) demultiplexer_8 (
    .out0(demultiplexer_8_out0), .out1(demultiplexer_8_out1), .in(multiplexer_6_out), .sel(f));
  assign and_1_out = demultiplexer_7_out0 & demultiplexer_8_out0;  // AND_Gate and_1, 16 bits wide
  Adder #(.width(16)) adder_1 (
    .a(demultiplexer_7_out1), .b(demultiplexer_8_out1), .out(adder_1_out));  // open: cin, cout
  Demultiplexer #(.width(16)) demultiplexer_9 (
    .out0(demultiplexer_9_out0), .out1(demultiplexer_9_out1), .in(multiplexer_7_out), .sel(no));
  Multiplexer #(.width(16)) multiplexer_7 (.in0(and_1_out), .in1(adder_1_out), .out(multiplexer_7_out), .sel(f));
  assign not_5_out = ~demultiplexer_9_out1;  // NOT_Gate not_5, 16 bits wide
  Multiplexer #(.width(16)) multiplexer_8 (.in0(demultiplexer_9_out0), .in1(not_5_out), .out(ruedi), .sel(no));
  Comparator #(.width(16)) comparator_1 (.a({16{1'b0}}), .b(ruedi), .gt(ng), .eq(zr));  // open: lt
endmodule
